// Logisim project project.circ as structural Verilog
module main (
  input  [3:0] column_number,
  input  [5:0] bus_0,
  input  bus_0_2
);

  wire _1a, cdm16_1_p2, cdm16_1_p3, cdm16_1_p5, cdm16_1_p6, cdm16_1_p7, cdm16_1_p8, cdm16_1_p9, cdm16_1_p10,
       cdm16_1_p11, cdm16_1_p12, cdm16_1_p13, cdm16_1_p14, cdm16_1_p15, cdm16_1_p16, cdm16_1_p17,
       cdm16_1_p18, Clear_out, clk, code, data, decoder_2_out0, decoder_2_out1, decoder_2_out2,
       decoder_2_out3, decoder_2_out4, decoder_2_out5, decoder_2_out6, decoder_2_out7, decoder_2_out8,
       decoder_2_out9, decoder_2_out10, decoder_2_out11, decoder_2_out12, decoder_2_out13, decoder_2_out14,
       decoder_2_out15, decoder_3_out0, decoder_3_out1, not_1_out, not_2_out;
  wire [15:0] _8a0, _8a1, _8a2, _8a3, _8a4, _8a5, _8a6, _8a7, _8a8, _8a9, _8aa, _8ab, _8ac, _8ad, _8ae, _8af,
       cdm16_1_p19, cdm16_1_p20, cdm16_1_p21, column, controlled_buffer_2_out;

  Clock clock_1 (.out(clk));
  DotMatrix #(.matrixcols(16), .matrixrows(16)) dotmatrix_1 (
    .col0(_8a0), .col1(_8a1), .col2(_8a2), .col3(_8a3), .col4(_8a4), .col5(_8a5), .col6(_8a6), .col7(_8a7),
    .col8(_8a8), .col9(_8a9), .col10(_8aa), .col11(_8ab), .col12(_8ac), .col13(_8ad), .col14(_8ae),
    .col15(_8af));
  DotMatrix #(.matrixcols(16), .matrixrows(16)) dotmatrix_2 ();  // open: col0, col1, col2, col3, col4, col5, col6, col7, col8, col9, col10, col11, col12, col13, col14, col15
  DotMatrix #(.matrixcols(16), .matrixrows(16)) dotmatrix_3 ();  // open: col0, col1, col2, col3, col4, col5, col6, col7, col8, col9, col10, col11, col12, col13, col14, col15
  DotMatrix #(.matrixcols(16), .matrixrows(16)) dotmatrix_4 ();  // open: col0, col1, col2, col3, col4, col5, col6, col7, col8, col9, col10, col11, col12, col13, col14, col15
  DotMatrix #(.matrixcols(16), .matrixrows(16)) dotmatrix_5 ();  // open: col0, col1, col2, col3, col4, col5, col6, col7, col8, col9, col10, col11, col12, col13, col14, col15
  DotMatrix #(.matrixcols(16), .matrixrows(16)) dotmatrix_6 ();  // open: col0, col1, col2, col3, col4, col5, col6, col7, col8, col9, col10, col11, col12, col13, col14, col15
  DotMatrix #(.matrixcols(16), .matrixrows(16)) dotmatrix_7 ();  // open: col0, col1, col2, col3, col4, col5, col6, col7, col8, col9, col10, col11, col12, col13, col14, col15
  DotMatrix #(.matrixcols(16), .matrixrows(16)) dotmatrix_8 ();  // open: col0, col1, col2, col3, col4, col5, col6, col7, col8, col9, col10, col11, col12, col13, col14, col15
  Keyboard keyboard_1 (.clk(clk), .clr(Clear_out));  // open: re, avail, data
  Button Clear (.out(Clear_out));
  Button Enter ();  // open: out
  DotMatrix #(.matrixcols(16), .matrixrows(16)) dotmatrix_9 ();  // open: col0, col1, col2, col3, col4, col5, col6, col7, col8, col9, col10, col11, col12, col13, col14, col15
  DotMatrix #(.matrixcols(16), .matrixrows(16)) dotmatrix_10 ();  // open: col0, col1, col2, col3, col4, col5, col6, col7, col8, col9, col10, col11, col12, col13, col14, col15
  DotMatrix #(.matrixcols(16), .matrixrows(16)) dotmatrix_11 ();  // open: col0, col1, col2, col3, col4, col5, col6, col7, col8, col9, col10, col11, col12, col13, col14, col15
  DotMatrix #(.matrixcols(16), .matrixrows(16)) dotmatrix_12 ();  // open: col0, col1, col2, col3, col4, col5, col6, col7, col8, col9, col10, col11, col12, col13, col14, col15
  DotMatrix #(.matrixcols(16), .matrixrows(16)) dotmatrix_13 ();  // open: col0, col1, col2, col3, col4, col5, col6, col7, col8, col9, col10, col11, col12, col13, col14, col15
  DotMatrix #(.matrixcols(16), .matrixrows(16)) dotmatrix_14 ();  // open: col0, col1, col2, col3, col4, col5, col6, col7, col8, col9, col10, col11, col12, col13, col14, col15
  DotMatrix #(.matrixcols(16), .matrixrows(16)) dotmatrix_15 ();  // open: col0, col1, col2, col3, col4, col5, col6, col7, col8, col9, col10, col11, col12, col13, col14, col15
  DotMatrix #(.matrixcols(16), .matrixrows(16)) dotmatrix_16 ();  // open: col0, col1, col2, col3, col4, col5, col6, col7, col8, col9, col10, col11, col12, col13, col14, col15
  DotMatrix #(.matrixcols(16), .matrixrows(16)) dotmatrix_17 ();  // open: col0, col1, col2, col3, col4, col5, col6, col7, col8, col9, col10, col11, col12, col13, col14, col15
  DotMatrix #(.matrixcols(16), .matrixrows(16)) dotmatrix_18 ();  // open: col0, col1, col2, col3, col4, col5, col6, col7, col8, col9, col10, col11, col12, col13, col14, col15
  DotMatrix #(.matrixcols(16), .matrixrows(16)) dotmatrix_19 ();  // open: col0, col1, col2, col3, col4, col5, col6, col7, col8, col9, col10, col11, col12, col13, col14, col15
  DotMatrix #(.matrixcols(16), .matrixrows(16)) dotmatrix_20 ();  // open: col0, col1, col2, col3, col4, col5, col6, col7, col8, col9, col10, col11, col12, col13, col14, col15
  DotMatrix #(.matrixcols(16), .matrixrows(16)) dotmatrix_21 ();  // open: col0, col1, col2, col3, col4, col5, col6, col7, col8, col9, col10, col11, col12, col13, col14, col15
  DotMatrix #(.matrixcols(16), .matrixrows(16)) dotmatrix_22 ();  // open: col0, col1, col2, col3, col4, col5, col6, col7, col8, col9, col10, col11, col12, col13, col14, col15
  DotMatrix #(.matrixcols(16), .matrixrows(16)) dotmatrix_23 ();  // open: col0, col1, col2, col3, col4, col5, col6, col7, col8, col9, col10, col11, col12, col13, col14, col15
  DotMatrix #(.matrixcols(16), .matrixrows(16)) dotmatrix_24 ();  // open: col0, col1, col2, col3, col4, col5, col6, col7, col8, col9, col10, col11, col12, col13, col14, col15
  // Probe on cdm16_1_p10
  // Probe on cdm16_1_p9
  // Probe on cdm16_1_p7
  // Probe on cdm16_1_p6
  // Probe on cdm16_1_p5
  // Probe on cdm16_1_p3
  // Probe on cdm16_1_p2
  DotMatrix #(.matrixcols(16), .matrixrows(16)) dotmatrix_25 ();  // open: col0, col1, col2, col3, col4, col5, col6, col7, col8, col9, col10, col11, col12, col13, col14, col15
  DotMatrix #(.matrixcols(16), .matrixrows(16)) dotmatrix_26 ();  // open: col0, col1, col2, col3, col4, col5, col6, col7, col8, col9, col10, col11, col12, col13, col14, col15
  DotMatrix #(.matrixcols(16), .matrixrows(16)) dotmatrix_27 ();  // open: col0, col1, col2, col3, col4, col5, col6, col7, col8, col9, col10, col11, col12, col13, col14, col15
  DotMatrix #(.matrixcols(16), .matrixrows(16)) dotmatrix_28 ();  // open: col0, col1, col2, col3, col4, col5, col6, col7, col8, col9, col10, col11, col12, col13, col14, col15
  DotMatrix #(.matrixcols(16), .matrixrows(16)) dotmatrix_29 ();  // open: col0, col1, col2, col3, col4, col5, col6, col7, col8, col9, col10, col11, col12, col13, col14, col15
  DotMatrix #(.matrixcols(16), .matrixrows(16)) dotmatrix_30 ();  // open: col0, col1, col2, col3, col4, col5, col6, col7, col8, col9, col10, col11, col12, col13, col14, col15
  DotMatrix #(.matrixcols(16), .matrixrows(16)) dotmatrix_31 ();  // open: col0, col1, col2, col3, col4, col5, col6, col7, col8, col9, col10, col11, col12, col13, col14, col15
  DotMatrix #(.matrixcols(16), .matrixrows(16)) dotmatrix_32 ();  // open: col0, col1, col2, col3, col4, col5, col6, col7, col8, col9, col10, col11, col12, col13, col14, col15
  // Probe on cdm16_1_p11
  // Probe on cdm16_1_p13
  // Probe on cdm16_1_p14
  // Probe on cdm16_1_p15
  // cdm16 cdm16_1: pin names not known; wires that end beside it: bus_0_2, cdm16_1_p2, cdm16_1_p3, clk, cdm16_1_p5, cdm16_1_p6, cdm16_1_p7, cdm16_1_p8, cdm16_1_p9, cdm16_1_p10, cdm16_1_p11, cdm16_1_p12, cdm16_1_p13, cdm16_1_p14, cdm16_1_p15, cdm16_1_p16, cdm16_1_p17, cdm16_1_p18, cdm16_1_p19, cdm16_1_p20, cdm16_1_p21
  LED led_1 (.in(cdm16_1_p12));
  // Probe on cdm16_1_p8
  Decoder decoder_1 (.out0(code), .out1(data), .sel(cdm16_1_p16), .en(cdm16_1_p17));
  not not_1 (not_1_out, cdm16_1_p18);
  assign cdm16_1_p21 = cdm16_1_p18 ? controlled_buffer_2_out : 16'bz;  // Controlled_Buffer controlled_buffer_1
  DotMatrix #(.matrixcols(16), .matrixrows(16)) dotmatrix_33 ();  // open: col0, col1, col2, col3, col4, col5, col6, col7, col8, col9, col10, col11, col12, col13, col14, col15
  DotMatrix #(.matrixcols(16), .matrixrows(16)) dotmatrix_34 ();  // open: col0, col1, col2, col3, col4, col5, col6, col7, col8, col9, col10, col11, col12, col13, col14, col15
  DotMatrix #(.matrixcols(16), .matrixrows(16)) dotmatrix_35 ();  // open: col0, col1, col2, col3, col4, col5, col6, col7, col8, col9, col10, col11, col12, col13, col14, col15
  DotMatrix #(.matrixcols(16), .matrixrows(16)) dotmatrix_36 ();  // open: col0, col1, col2, col3, col4, col5, col6, col7, col8, col9, col10, col11, col12, col13, col14, col15
  DotMatrix #(.matrixcols(16), .matrixrows(16)) dotmatrix_37 ();  // open: col0, col1, col2, col3, col4, col5, col6, col7, col8, col9, col10, col11, col12, col13, col14, col15
  DotMatrix #(.matrixcols(16), .matrixrows(16)) dotmatrix_38 ();  // open: col0, col1, col2, col3, col4, col5, col6, col7, col8, col9, col10, col11, col12, col13, col14, col15
  DotMatrix #(.matrixcols(16), .matrixrows(16)) dotmatrix_39 ();  // open: col0, col1, col2, col3, col4, col5, col6, col7, col8, col9, col10, col11, col12, col13, col14, col15
  DotMatrix #(.matrixcols(16), .matrixrows(16)) dotmatrix_40 ();  // open: col0, col1, col2, col3, col4, col5, col6, col7, col8, col9, col10, col11, col12, col13, col14, col15
  assign controlled_buffer_2_out = not_1_out ? cdm16_1_p20 : 16'bz;  // Controlled_Buffer controlled_buffer_2
  not not_2 (not_2_out, code);
  DotMatrix #(.matrixcols(16), .matrixrows(16)) dotmatrix_41 ();  // open: col0, col1, col2, col3, col4, col5, col6, col7, col8, col9, col10, col11, col12, col13, col14, col15
  DotMatrix #(.matrixcols(16), .matrixrows(16)) dotmatrix_42 ();  // open: col0, col1, col2, col3, col4, col5, col6, col7, col8, col9, col10, col11, col12, col13, col14, col15
  DotMatrix #(.matrixcols(16), .matrixrows(16)) dotmatrix_43 ();  // open: col0, col1, col2, col3, col4, col5, col6, col7, col8, col9, col10, col11, col12, col13, col14, col15
  DotMatrix #(.matrixcols(16), .matrixrows(16)) dotmatrix_44 ();  // open: col0, col1, col2, col3, col4, col5, col6, col7, col8, col9, col10, col11, col12, col13, col14, col15
  DotMatrix #(.matrixcols(16), .matrixrows(16)) dotmatrix_45 ();  // open: col0, col1, col2, col3, col4, col5, col6, col7, col8, col9, col10, col11, col12, col13, col14, col15
  DotMatrix #(.matrixcols(16), .matrixrows(16)) dotmatrix_46 ();  // open: col0, col1, col2, col3, col4, col5, col6, col7, col8, col9, col10, col11, col12, col13, col14, col15
  DotMatrix #(.matrixcols(16), .matrixrows(16)) dotmatrix_47 ();  // open: col0, col1, col2, col3, col4, col5, col6, col7, col8, col9, col10, col11, col12, col13, col14, col15
  DotMatrix #(.matrixcols(16), .matrixrows(16)) dotmatrix_48 ();  // open: col0, col1, col2, col3, col4, col5, col6, col7, col8, col9, col10, col11, col12, col13, col14, col15
  ROM #(.addrWidth(16), .dataWidth(16)) rom_1 (.addr(cdm16_1_p19), .data(controlled_buffer_2_out), .sel(not_2_out));
  RAM #(.addrWidth(16), .dataWidth(16)) ram_1 (
    .addr(cdm16_1_p19), .data(controlled_buffer_2_out), .sel(data), .clk(clk), .ld(cdm16_1_p18));  // open: clr
  DotMatrix #(.matrixcols(16), .matrixrows(16)) dotmatrix_49 ();  // open: col0, col1, col2, col3, col4, col5, col6, col7, col8, col9, col10, col11, col12, col13, col14, col15
  DotMatrix #(.matrixcols(16), .matrixrows(16)) dotmatrix_50 ();  // open: col0, col1, col2, col3, col4, col5, col6, col7, col8, col9, col10, col11, col12, col13, col14, col15
  DotMatrix #(.matrixcols(16), .matrixrows(16)) dotmatrix_51 ();  // open: col0, col1, col2, col3, col4, col5, col6, col7, col8, col9, col10, col11, col12, col13, col14, col15
  DotMatrix #(.matrixcols(16), .matrixrows(16)) dotmatrix_52 ();  // open: col0, col1, col2, col3, col4, col5, col6, col7, col8, col9, col10, col11, col12, col13, col14, col15
  DotMatrix #(.matrixcols(16), .matrixrows(16)) dotmatrix_53 ();  // open: col0, col1, col2, col3, col4, col5, col6, col7, col8, col9, col10, col11, col12, col13, col14, col15
  DotMatrix #(.matrixcols(16), .matrixrows(16)) dotmatrix_54 ();  // open: col0, col1, col2, col3, col4, col5, col6, col7, col8, col9, col10, col11, col12, col13, col14, col15
  DotMatrix #(.matrixcols(16), .matrixrows(16)) dotmatrix_55 ();  // open: col0, col1, col2, col3, col4, col5, col6, col7, col8, col9, col10, col11, col12, col13, col14, col15
  DotMatrix #(.matrixcols(16), .matrixrows(16)) dotmatrix_56 ();  // open: col0, col1, col2, col3, col4, col5, col6, col7, col8, col9, col10, col11, col12, col13, col14, col15
  DotMatrix #(.matrixcols(16), .matrixrows(16)) dotmatrix_57 ();  // open: col0, col1, col2, col3, col4, col5, col6, col7, col8, col9, col10, col11, col12, col13, col14, col15
  DotMatrix #(.matrixcols(16), .matrixrows(16)) dotmatrix_58 ();  // open: col0, col1, col2, col3, col4, col5, col6, col7, col8, col9, col10, col11, col12, col13, col14, col15
  DotMatrix #(.matrixcols(16), .matrixrows(16)) dotmatrix_59 ();  // open: col0, col1, col2, col3, col4, col5, col6, col7, col8, col9, col10, col11, col12, col13, col14, col15
  DotMatrix #(.matrixcols(16), .matrixrows(16)) dotmatrix_60 ();  // open: col0, col1, col2, col3, col4, col5, col6, col7, col8, col9, col10, col11, col12, col13, col14, col15
  DotMatrix #(.matrixcols(16), .matrixrows(16)) dotmatrix_61 ();  // open: col0, col1, col2, col3, col4, col5, col6, col7, col8, col9, col10, col11, col12, col13, col14, col15
  DotMatrix #(.matrixcols(16), .matrixrows(16)) dotmatrix_62 ();  // open: col0, col1, col2, col3, col4, col5, col6, col7, col8, col9, col10, col11, col12, col13, col14, col15
  DotMatrix #(.matrixcols(16), .matrixrows(16)) dotmatrix_63 ();  // open: col0, col1, col2, col3, col4, col5, col6, col7, col8, col9, col10, col11, col12, col13, col14, col15
  DotMatrix #(.matrixcols(16), .matrixrows(16)) dotmatrix_64 ();  // open: col0, col1, col2, col3, col4, col5, col6, col7, col8, col9, col10, col11, col12, col13, col14, col15
  Register #(.width(16)) register_1 (.D(column), .en(decoder_2_out0), .Q(_8a0));  // open: clk, clr
  Register #(.width(16)) register_2 (.D(column), .en(decoder_2_out1), .Q(_8a1));  // open: clk, clr
  Register #(.width(16)) register_3 (.D(column), .en(decoder_2_out2), .Q(_8a2));  // open: clk, clr
  Register #(.width(16)) register_4 (.D(column), .en(decoder_2_out4), .Q(_8a4));  // open: clk, clr
  Register #(.width(16)) register_5 (.D(column), .en(decoder_2_out3), .Q(_8a3));  // open: clk, clr
  Register #(.width(16)) register_6 (.D(column), .en(decoder_2_out5), .Q(_8a5));  // open: clk, clr
  Decoder #(.select(4), .disabled(0)) decoder_2 (
    .out0(decoder_2_out0), .out1(decoder_2_out1), .out2(decoder_2_out2), .out3(decoder_2_out3),
    .out4(decoder_2_out4), .out5(decoder_2_out5), .out6(decoder_2_out6), .out7(decoder_2_out7),
    .out8(decoder_2_out8), .out9(decoder_2_out9), .out10(decoder_2_out10), .out11(decoder_2_out11),
    .out12(decoder_2_out12), .out13(decoder_2_out13), .out14(decoder_2_out14), .out15(decoder_2_out15),
    .sel(column_number), .en(_1a));
  Register #(.width(16)) register_7 (.D(column), .en(decoder_2_out6), .Q(_8a6));  // open: clk, clr
  Register #(.width(16)) register_8 (.D(column), .en(decoder_2_out7));  // open: Q, clk, clr
  Register #(.width(16)) register_9 (.D(column), .en(decoder_2_out8));  // open: Q, clk, clr
  Register #(.width(16)) register_10 (.D(column), .en(decoder_2_out9));  // open: Q, clk, clr
  Register #(.width(16)) register_11 (.D(column), .en(decoder_2_out10));  // open: Q, clk, clr
  Decoder decoder_3 (.out0(decoder_3_out0), .out1(decoder_3_out1), .sel(bus_0[5]));  // open: en
  Register #(.width(16)) register_12 (.D(column), .en(decoder_2_out11));  // open: Q, clk, clr
  Register #(.width(16)) register_13 (.D(column), .en(decoder_2_out12));  // open: Q, clk, clr
  Decoder #(.select(5), .disabled(0)) decoder_4 (
    .out0(_1a), .sel(bus_0[4:0]), .en(decoder_3_out0));  // open: out1, out2, out3, out4, out5, out6, out7, out8, out9, out10, out11, out12, out13, out14, out15, out16, out17, out18, out19, out20, out21, out22, out23, out24, out25, out26, out27, out28, out29, out30, out31
  Decoder #(.select(5), .disabled(0)) decoder_5 (
    .sel(bus_0[4:0]), .en(decoder_3_out1));  // open: out0, out1, out2, out3, out4, out5, out6, out7, out8, out9, out10, out11, out12, out13, out14, out15, out16, out17, out18, out19, out20, out21, out22, out23, out24, out25, out26, out27, out28, out29, out30, out31
  Register #(.width(16)) register_14 (.D(column), .en(decoder_2_out13));  // open: Q, clk, clr
  Register #(.width(16)) register_15 (.D(column), .en(decoder_2_out14));  // open: Q, clk, clr
  Register #(.width(16)) register_16 (.D(column), .en(decoder_2_out15));  // open: Q, clk, clr
endmodule

module asset_memory (
  input  [15:0] addr,
  input  [15:0] column,
  input  clock,
  input  \end 
);
endmodule
